// Digital circuit IF.dig as structural Verilog
module IF (
  input  clk,
  input  pw,
  input  rs,
  input  [31:0] ad,
  output [31:0] ir,
  output [31:0] pc
);

  fb_pc #(.applicationType("IVERILOG"), .iverilogOptions("-y /Users/zhangyibo/riscvdesign/RISCVFirebird/Pipeline/rtl\n-I /Users/zhangyibo/riscvdesign/RISCVFirebird/Pipeline/rtl"), .CodeFile("/Users/zhangyibo/riscvdesign/RISCVFirebird/Pipeline/rtl/fb_pc.v")) u_fb_pc (
    .pc_write(pw), .clk(clk), .pc_reset(rs), .new_address(ad), .out_address(pc));
  ROM #(.AddrBits(10), .Bits(32)) instmem (.A(pc[9:0]), .sel(1'b1), .D(ir));

  // Notes on the sheet:
  //   clk: pin 2
  //   pw: 用于在插入气泡的时候锁住pc, pin 1
  //   rs: 用于重置pc, pin 3
  //   ir: 输出是指令寄存器中取出的指令, pin 5
  //   ad: 输入的32位pc新地址
  //   来源包括：pc自增或是分支指令的目的地址, pin 4
  //   pc: pc寄存器的数值, pin 6
  //   contents of instmem (hex, n*v repeats v):
  //   4000ef
endmodule
