// Digital circuit ROOT.dig as structural Verilog
module ROOT (
  input  _1,
  input  _0,
  input  clk
);

  wire alusrc, alusrc1, arsrc, bra, bra1, CF, e2, embra, emmr, emmtr, emmw, emrs2d, emrw, fb_fwdmux_2_p5,
       idexreg_1_p27, idexreg_1_p28, imm, lk, memwbreg_1_p10, memwbreg_1_p11, mr, mr1, mtr, mtr1,
       multiplexer_3_out, mw, mw1, mwmtr, NF, pca1, pca11, ramdualport_1_d, rst, rw, rw1, u_fb_alu_csr_write,
       VF, ZF;
  wire [1:0] aluop, emalur, fa, fb;
  wire [3:0] u_fb_alu_csr;
  wire [4:0] emrd, memwbreg_1_p12, mwrw, rdd, rs11, rs22;
  wire [18:0] aluct, u_fb_alu_ctrl_alu_control;
  wire [31:0] fb_fwdmux_1_p5, if_1_ir, immj, inst, multiplexer_2_out, opc, pc, pcn, rbval, u_fb_alu_alu_res,
       u_fb_regfile_rdata1, u_fb_regfile_rdata2;

  IF if_1 (.clk(clk), .pw(lk), .rs(_0), .ir(if_1_ir), .pc(pc));  // open: ad
  Add #(.Bits(32)) adderpc (.a(pc), .b(32'h1), .c_i(_0), .s(pcn), .c_o(_0));
  fb_hazard_detection_unit #(.applicationType("IVERILOG"), .iverilogOptions("-I /Users/zhangyibo/riscvdesign/RISCVFirebird/Pipeline/rtl\n-y/Users/zhangyibo/riscvdesign/RISCVFirebird/Pipeline/rtl"), .CodeFile("/Users/zhangyibo/riscvdesign/RISCVFirebird/Pipeline/rtl/fb_hazard_detection_unit.v")) u_fb_hazard_detection_unit (
    .id_ex_memread(mr1), .id_ex_register_rd(rdd), .inst(inst[9:0]), .lock(lk));
  // IFIDReg ifidreg_1: pin names not known; wires that end beside it: clk, lk, _1, rst, pc, pcn, if_1_ir, opc, inst, pca1
  RAMDualPort ramdualport_1 (.A(emalur), .Din(emrs2d), .str(emmw), .C(clk), .ld(emmr), .D(ramdualport_1_d));
  fb_cu #(.applicationType("IVERILOG"), .iverilogOptions("-I /Users/zhangyibo/riscvdesign/RISCVFirebird/Pipeline/rtl\n-y/Users/zhangyibo/riscvdesign/RISCVFirebird/Pipeline/rtl"), .CodeFile("/Users/zhangyibo/riscvdesign/RISCVFirebird/Pipeline/rtl/fb_cu.v")) u_fb_cu (
    .opcode(inst[6:0]), .alu_op(aluop), .alu_src(alusrc), .alu_res_src(arsrc), .mem_read(mr), .mem_write(mw),
    .branch(bra), .mem_to_reg(mtr), .reg_write(rw));
  fb_alu_ctrl #(.applicationType("IVERILOG"), .iverilogOptions("-I /Users/zhangyibo/riscvdesign/RISCVFirebird/Pipeline/rtl\n-y/Users/zhangyibo/riscvdesign/RISCVFirebird/Pipeline/rtl"), .CodeFile("/Users/zhangyibo/riscvdesign/RISCVFirebird/Pipeline/rtl/fb_alu_ctrl.v")) u_fb_alu_ctrl (
    .alu_op(aluop), .func7(inst[31:25]), .func3(inst[14:12]), .alu_control(u_fb_alu_ctrl_alu_control));
  fb_regfile #(.applicationType("IVERILOG"), .iverilogOptions("-I /Users/zhangyibo/riscvdesign/RISCVFirebird/Pipeline/rtl\n-y/Users/zhangyibo/riscvdesign/RISCVFirebird/Pipeline/rtl"), .CodeFile("/Users/zhangyibo/riscvdesign/RISCVFirebird/Pipeline/rtl/fb_regfile.v")) u_fb_regfile (
    .clk(clk), .raddr1(inst[19:15]), .raddr2(inst[24:20]), .we(_1), .waddr(mwrw), .wdata(rbval),
    .rdata1(u_fb_regfile_rdata1), .rdata2(u_fb_regfile_rdata2));  // open: reset
  fb_imm_gen #(.applicationType("IVERILOG"), .iverilogOptions("-I /Users/zhangyibo/riscvdesign/RISCVFirebird/Pipeline/rtl\n-y/Users/zhangyibo/riscvdesign/RISCVFirebird/Pipeline/rtl"), .CodeFile("/Users/zhangyibo/riscvdesign/RISCVFirebird/Pipeline/rtl/fb_imm_gen.v")) u_fb_imm_gen (
    .inst(inst), .imm(immj));
  // IDEXReg idexreg_1: pin names not known; wires that end beside it: clk, _1, rst, alusrc, arsrc, mr, mw, bra, mtr, rw, pca1, u_fb_regfile_rdata1, u_fb_regfile_rdata2, immj, inst[19:15], inst[24:20], inst[11:7], u_fb_alu_ctrl_alu_control, alusrc1, e2, mr1, mw1, bra1, mtr1, rw1, pca11, idexreg_1_p27, idexreg_1_p28, imm, rs11, rs22, rdd, aluct
  // MEMWBReg memwbreg_1: pin names not known; wires that end beside it: clk, _1, emmtr, emrw, ramdualport_1_d, emalur, emrd, mwmtr, mwrw, memwbreg_1_p10, memwbreg_1_p11, memwbreg_1_p12
  fb_forwarding_unit #(.applicationType("IVERILOG"), .iverilogOptions("-I /Users/zhangyibo/riscvdesign/RISCVFirebird/Pipeline/rtl\n-y/Users/zhangyibo/riscvdesign/RISCVFirebird/Pipeline/rtl"), .CodeFile("/Users/zhangyibo/riscvdesign/RISCVFirebird/Pipeline/rtl/fb_forwarding_unit.v")) u_fb_forwarding_unit (
    .id_ex_register_rs1(rs11), .id_ex_register_rs2(rs22), .ex_mem_regwrite(emrw), .ex_mem_register_rd(emrd),
    .mem_wb_register_rd(memwbreg_1_p12), .forward_a(fa), .forward_b(fb));  // open: mem_wb_regwrite
  fb_ctrl_hazard_unit #(.applicationType("IVERILOG"), .iverilogOptions("-I /Users/zhangyibo/riscvdesign/RISCVFirebird/Pipeline/rtl\n-y/Users/zhangyibo/riscvdesign/RISCVFirebird/Pipeline/rtl"), .CodeFile("/Users/zhangyibo/riscvdesign/RISCVFirebird/Pipeline/rtl/fb_ctrl_hazard_unit.v")) u_fb_ctrl_hazard_unit (
    .pc(opc), .inst(inst), .imm(immj), .branch(embra), .NF(NF), .ZF(ZF), .CF(CF), .VF(VF), .register_rst(rst));  // open: address_src, predict_pc, predict_err_pc
  // fb_fwdmux fb_fwdmux_1: pin names not known; wires that end beside it: fa, idexreg_1_p27, emalur, rbval, fb_fwdmux_1_p5
  // fb_fwdmux fb_fwdmux_2: pin names not known; wires that end beside it: fb, idexreg_1_p28, emalur, rbval, fb_fwdmux_2_p5
  Multiplexer multiplexer_1 (.sel(mwmtr), .in_0(memwbreg_1_p11), .in_1(memwbreg_1_p10), .out(rbval[0]));
  Multiplexer multiplexer_2 (.sel(alusrc1), .in_0(fb_fwdmux_2_p5), .in_1(imm), .out(multiplexer_2_out[0]));
  fb_alu #(.applicationType("IVERILOG"), .iverilogOptions("-I /Users/zhangyibo/riscvdesign/RISCVFirebird/Pipeline/rtl\n-y/Users/zhangyibo/riscvdesign/RISCVFirebird/Pipeline/rtl"), .CodeFile("/Users/zhangyibo/riscvdesign/RISCVFirebird/Pipeline/rtl/fb_alu.v")) u_fb_alu (
    .alu_control(aluct), .op1(fb_fwdmux_1_p5), .op2(multiplexer_2_out), .alu_res(u_fb_alu_alu_res),
    .csr(u_fb_alu_csr), .csr_write(u_fb_alu_csr_write));
  fb_csr #(.applicationType("IVERILOG"), .iverilogOptions("-I /Users/zhangyibo/riscvdesign/RISCVFirebird/Pipeline/rtl\n-y/Users/zhangyibo/riscvdesign/RISCVFirebird/Pipeline/rtl"), .CodeFile("/Users/zhangyibo/riscvdesign/RISCVFirebird/Pipeline/rtl/fb_csr.v")) u_fb_csr (
    .clk(clk), .we(u_fb_alu_csr_write), .csr(u_fb_alu_csr), .NF(NF), .ZF(ZF), .CF(CF), .VF(VF));
  Multiplexer multiplexer_3 (.sel(e2), .in_0(u_fb_alu_alu_res[0]), .in_1(pca11), .out(multiplexer_3_out));
  // EXMEMReg exmemreg_1: pin names not known; wires that end beside it: clk, _1, rst, mr1, mw1, bra1, mtr1, rw1, multiplexer_3_out, fb_fwdmux_2_p5, rdd, emmr, emmw, embra, emmtr, emrw, emalur, emrs2d, emrd
  // Pins of 10 and 32 bits meet at inst
  // Pins of 1 and 32 bits meet at rbval
  // Pins of 1 and 32 bits meet at multiplexer_2_out
  // Pins of 1 and 32 bits meet at u_fb_alu_alu_res

  // Other names for the same wires on the sheet: rd[4:0] = inst[11:7]; rs1[4:0] = inst[19:15]; rs2[4:0] = inst[24:20];
  //   gcc = _1; gnd = _0

  // Notes on the sheet:
  //   _1: 默认使用的高电平, default 1
  //   _0: 低电平
endmodule
